// Logisim project Project.circ as structural Verilog: 21 circuits, main circuit main
module main (
);

  wire branch_1_condition, clock_1_out, control_unit_1_branch, control_unit_1_immediate, control_unit_1_load,
       control_unit_1_memory_read, control_unit_1_memory_write, control_unit_1_pcmux, control_unit_1_pcwrite,
       control_unit_1_regwrite, multiplexer_2_out;
  wire [1:0] control_unit_1_store;
  wire [3:0] control_unit_1_alu_control, multiplexer_4_out, multiplexer_5_out;
  wire [19:0] adder_1_out, adder_2_out, adder_3_out, alu_1_result, extender_5_20_1_out_2, multiplexer_1_out,
       multiplexer_3_out, multiplexer_6_out, PC_q, ram_1_data, Register_File_address_a_out,
       Register_File_address_b_out, rom_1_data, sign_extend_7_20_1_extend_number, sign_extender_16_20_1_out_2;

  Multiplexer #(.width(20), .enable("false")) multiplexer_1 (
    .in0(adder_1_out), .in1(multiplexer_3_out), .out(multiplexer_1_out), .sel(multiplexer_2_out));
  Multiplexer #(.enable("false")) multiplexer_2 (
    .in0(control_unit_1_pcmux), .in1(branch_1_condition), .out(multiplexer_2_out), .sel(control_unit_1_branch));
  Adder #(.width(20)) adder_1 (.a(20'h1), .b(PC_q), .out(adder_1_out), .cin(1'b0));  // open: cout
  Register #(.width(20)) PC (
    .D(multiplexer_1_out), .en(control_unit_1_pcwrite), .Q(PC_q), .clk(clock_1_out));  // open: clr
  Multiplexer #(.width(20), .enable("false")) multiplexer_3 (
    .in0(adder_2_out), .in1(adder_3_out), .out(multiplexer_3_out), .sel(control_unit_1_branch));
  Clock clock_1 (.out(clock_1_out));
  Adder #(.width(20)) adder_2 (.a(PC_q), .b(sign_extender_16_20_1_out_2), .out(adder_2_out), .cin(1'b0));  // open: cout
  Adder #(.width(20)) adder_3 (.a(PC_q), .b(extender_5_20_1_out_2), .out(adder_3_out), .cin(1'b0));  // open: cout
  ROM #(.addrWidth(20), .dataWidth(20)) rom_1 (.addr(PC_q), .data(rom_1_data), .sel(1'b1));
  Extender_5_20 extender_5_20_1 (.in_1({rom_1_data[15], rom_1_data[3:0]}), .out_2(extender_5_20_1_out_2));
  Control_Unit control_unit_1 (
    .in_1(rom_1_data), .Clock(clock_1_out), .Immediate(control_unit_1_immediate),
    .ALU_Control(control_unit_1_alu_control), .Load(control_unit_1_load),
    .Memory_Read(control_unit_1_memory_read), .Memory_Write(control_unit_1_memory_write),
    .RegWrite(control_unit_1_regwrite), .PCmux(control_unit_1_pcmux), .PCwrite(control_unit_1_pcwrite),
    .Branch(control_unit_1_branch), .Store(control_unit_1_store[0]));
  not not_1 (control_unit_1_store[1], control_unit_1_branch);
  Multiplexer #(.select(2), .width(4), .enable("false")) multiplexer_4 (
    .in0(rom_1_data[10:7]), .in2(rom_1_data[11:8]), .in3(rom_1_data[15:12]), .out(multiplexer_4_out),
    .sel(control_unit_1_store));  // open: in1
  Multiplexer #(.width(4), .enable("false")) multiplexer_5 (
    .in0(rom_1_data[14:11]), .in1(rom_1_data[3:0]), .out(multiplexer_5_out), .sel(control_unit_1_store[1]));
  Sign_Extender_16_20 sign_extender_16_20_1 (.in_1(rom_1_data[15:0]), .out_2(sign_extender_16_20_1_out_2));
  Multiplexer #(.width(20), .enable("false")) multiplexer_6 (
    .in0(alu_1_result), .in1(ram_1_data), .out(multiplexer_6_out), .sel(control_unit_1_load));
  Sign_Extend_7_20 sign_extend_7_20_1 (
    .Immediate_value({rom_1_data[0], rom_1_data[1], rom_1_data[2], rom_1_data[3], rom_1_data[4], rom_1_data[5], rom_1_data[6]}),
    .Extend_number(sign_extend_7_20_1_extend_number));
  Register_File Register_File (
    .Data_in(multiplexer_6_out), .Load(control_unit_1_regwrite), .Input(rom_1_data[15:12]),
    .Clock(clock_1_out), .Address_A_out(Register_File_address_a_out),
    .Address_B_out(Register_File_address_b_out), .Adress_A(multiplexer_4_out), .Adress_B(multiplexer_5_out));
  Branch branch_1 (
    .nzp(rom_1_data[6:4]), .OP1(Register_File_address_a_out), .OP2(Register_File_address_b_out),
    .Condition(branch_1_condition));
  ALU alu_1 (
    .SRC1(Register_File_address_a_out), .SRC2(Register_File_address_b_out),
    .Immediate(sign_extend_7_20_1_extend_number), .S(control_unit_1_immediate), .result(alu_1_result),
    .ALU_control(control_unit_1_alu_control));
  RAM #(.addrWidth(10), .dataWidth(20), .bus("separate")) ram_1 (
    .addr(rom_1_data[9:0]), .din(Register_File_address_a_out), .data(ram_1_data),
    .str(control_unit_1_memory_write), .sel(1'b1), .clk(clock_1_out), .ld(control_unit_1_memory_read),
    .clr(1'b0));

  // Notes on the sheet:
  //   contents of rom_1 (hex, n*v repeats v):
  //   1009a 1119a 12297 133fb 24300 35201 46103 17506 68001 69004 6a00f 6b007 70003 72006 78011 72007
  //   6c009 6d012 6e000 6f00b 842a2 12284 8c41f 5ffe9
endmodule

// 1-A
module _1_bit_Full_Adder (
  input  Carry_In,
  input  a,
  input  b,
  output sum,
  output Carry_out
);

  wire and_1_out, and_2_out, and_3_out;

  xor xor_1 (sum, Carry_In, a, b);
  and and_1 (and_1_out, Carry_In, a);
  and and_2 (and_2_out, Carry_In, b);
  and and_3 (and_3_out, a, b);
  or or_1 (Carry_out, and_1_out, and_2_out, and_3_out);
endmodule

// 4-Adder
module _4_bit_Adder (
  input  Carry_in,
  input  [3:0] A,
  input  [3:0] B,
  output [3:0] sum,
  output Carry_out
);

  wire n1_bit_full_adder_1_carry_out, n1_bit_full_adder_2_carry_out, n1_bit_full_adder_3_carry_out;

  _1_bit_Full_Adder u_1_bit_full_adder_1 (
    .Carry_In(Carry_in), .a(A[0]), .b(B[0]), .sum(sum[0]), .Carry_out(n1_bit_full_adder_1_carry_out));
  _1_bit_Full_Adder u_1_bit_full_adder_2 (
    .Carry_In(n1_bit_full_adder_1_carry_out), .a(A[1]), .b(B[1]), .sum(sum[1]),
    .Carry_out(n1_bit_full_adder_2_carry_out));
  _1_bit_Full_Adder u_1_bit_full_adder_3 (
    .Carry_In(n1_bit_full_adder_2_carry_out), .a(A[2]), .b(B[2]), .sum(sum[2]),
    .Carry_out(n1_bit_full_adder_3_carry_out));
  _1_bit_Full_Adder u_1_bit_full_adder_4 (
    .Carry_In(n1_bit_full_adder_3_carry_out), .a(A[3]), .b(B[3]), .sum(sum[3]), .Carry_out(Carry_out));
endmodule

// Adder
module _20_bit_Adder (
  input  [19:0] in_1,
  input  [19:0] in_2,
  output [19:0] sum,
  output out_4
);

  wire n4_bit_adder_1_carry_out, n4_bit_adder_2_carry_out, n4_bit_adder_3_carry_out, n4_bit_adder_4_carry_out;

  _4_bit_Adder u_4_bit_adder_1 (
    .Carry_in(1'b0), .A(in_1[3:0]), .B(in_2[3:0]), .Carry_out(n4_bit_adder_1_carry_out), .sum(sum[3:0]));
  _4_bit_Adder u_4_bit_adder_2 (
    .Carry_in(n4_bit_adder_1_carry_out), .A(in_1[7:4]), .B(in_2[7:4]), .Carry_out(n4_bit_adder_2_carry_out),
    .sum(sum[7:4]));
  _4_bit_Adder u_4_bit_adder_3 (
    .Carry_in(n4_bit_adder_2_carry_out), .A(in_1[11:8]), .B(in_2[11:8]),
    .Carry_out(n4_bit_adder_3_carry_out), .sum(sum[11:8]));
  _4_bit_Adder u_4_bit_adder_4 (
    .Carry_in(n4_bit_adder_3_carry_out), .A(in_1[15:12]), .B(in_2[15:12]),
    .Carry_out(n4_bit_adder_4_carry_out), .sum(sum[15:12]));
  _4_bit_Adder u_4_bit_adder_5 (
    .Carry_in(n4_bit_adder_4_carry_out), .A(in_1[19:16]), .B(in_2[19:16]), .Carry_out(out_4), .sum(sum[19:16]));
endmodule

module ALU (
  input  [19:0] SRC1,
  input  [19:0] SRC2,
  input  [19:0] Immediate,
  input  [3:0] ALU_control,
  input  S,
  output [19:0] result
);

  wire n20_bit_adder_1_out_4;
  wire [19:0] and_1_out, multiplexer_1_out, n20_bit_adder_1_sum, or_1_out, xor_1_out;

  Multiplexer #(.width(20), .enable("false")) multiplexer_1 (
    .in0(SRC2), .in1(Immediate), .out(multiplexer_1_out), .sel(S));
  assign xor_1_out = multiplexer_1_out ^ SRC1;  // XOR_Gate xor_1, 20 bits wide
  assign or_1_out = multiplexer_1_out | SRC1;  // OR_Gate or_1, 20 bits wide
  assign and_1_out = multiplexer_1_out & SRC1;  // AND_Gate and_1, 20 bits wide
  _20_bit_Adder u_20_bit_adder_1 (
    .in_1(multiplexer_1_out), .in_2(SRC1), .sum(n20_bit_adder_1_sum), .out_4(n20_bit_adder_1_out_4));
  Multiplexer #(.select(4), .width(20), .enable("false")) multiplexer_2 (
    .in0({20{1'b0}}), .in1(n20_bit_adder_1_sum), .in2(and_1_out), .in3(or_1_out), .in4(xor_1_out),
    .out(result), .sel(ALU_control));  // open: in5, in6, in7, in8, in9, in10, in11, in12, in13, in14, in15
  // also tied to GND on the sheet: n20_bit_adder_1_out_4
endmodule

// D flip flop
module D_flip_flop (
  input  D,
  input  Clock,
  input  Enable,
  output out_4
);

  wire d_latch_1_q, not_1_out;

  D_latch d_latch_1 (.D(D), .Clock(Clock), .Q(d_latch_1_q), .Enable(Enable));
  not not_1 (not_1_out, Clock);
  D_latch d_latch_2 (.D(d_latch_1_q), .Clock(not_1_out), .Q(out_4), .Enable(Enable));
endmodule

module D_latch (
  input  D,
  input  Clock,
  input  Enable,
  output Q
);

  wire and_1_out, and_2_out, nor_1_out, not_1_out;

  not not_1 (not_1_out, D);
  and and_1 (and_1_out, D, Enable, Clock);
  and and_2 (and_2_out, Clock, Enable, not_1_out);
  nor nor_1 (nor_1_out, and_1_out, Q);
  nor nor_2 (Q, nor_1_out, and_2_out);
endmodule

// Register
module _4_bit_Register (
  input  [3:0] Input,
  input  Enable,
  input  Clock,
  output [3:0] Output
);

  D_flip_flop d_flip_flop_1 (.D(Input[0]), .Clock(Clock), .out_4(Output[0]), .Enable(Enable));
  D_flip_flop d_flip_flop_2 (.D(Input[1]), .Clock(Clock), .out_4(Output[1]), .Enable(Enable));
  D_flip_flop d_flip_flop_3 (.D(Input[2]), .Clock(Clock), .out_4(Output[2]), .Enable(Enable));
  D_flip_flop d_flip_flop_4 (.D(Input[3]), .Clock(Clock), .out_4(Output[3]), .Enable(Enable));
endmodule

// Register
module _20_bit_Register (
  input  [19:0] Input,
  input  Enable,
  input  Clock,
  output [19:0] out_4
);

  _4_bit_Register u_4_bit_register_1 (.Input(Input[3:0]), .Clock(Clock), .Output(out_4[3:0]), .Enable(Enable));
  _4_bit_Register u_4_bit_register_2 (.Input(Input[7:4]), .Clock(Clock), .Output(out_4[7:4]), .Enable(Enable));
  _4_bit_Register u_4_bit_register_3 (.Input(Input[11:8]), .Clock(Clock), .Output(out_4[11:8]), .Enable(Enable));
  _4_bit_Register u_4_bit_register_4 (.Input(Input[15:12]), .Clock(Clock), .Output(out_4[15:12]), .Enable(Enable));
  _4_bit_Register u_4_bit_register_5 (.Input(Input[19:16]), .Clock(Clock), .Output(out_4[19:16]), .Enable(Enable));
endmodule

module Control_Unit (
  input  [19:0] in_1,
  input  Clock,
  output Immediate,
  output PCwrite,
  output RegWrite,
  output Load,
  output Memory_Read,
  output Memory_Write,
  output Branch,
  output [3:0] ALU_Control,
  output PCmux,
  output Store
);

  wire decoder_1_out1, decoder_1_out2, decoder_1_out3, decoder_1_out4, decoder_1_out10, or_2_out;
  wire [1:1] or_1_out;
  wire [3:0] multiplexer_1_out, register_1_q;

  Multiplexer #(.select(2), .width(4), .enable("false")) multiplexer_1 (
    .in0(in_1[19:16]), .in1(4'b1010), .in2(4'b0000), .out(multiplexer_1_out), .sel({or_1_out[1], Memory_Read}));  // open: in3
  Register #(.width(4)) register_1 (.D(multiplexer_1_out), .en(1'b1), .Q(register_1_q), .clk(Clock));  // open: clr
  or or_1 (or_1_out[1], decoder_1_out10, PCwrite);
  Decoder #(.select(4), .enable("false")) decoder_1 (
    .out1(decoder_1_out1), .out2(decoder_1_out2), .out3(decoder_1_out3), .out4(decoder_1_out4), .out5(PCmux),
    .out6(Memory_Read), .out7(Memory_Write), .out8(Branch), .out10(decoder_1_out10), .sel(register_1_q));  // open: out0, out9, out11, out12, out13, out14, out15
  or or_2 (or_2_out, decoder_1_out1, decoder_1_out2, decoder_1_out3, decoder_1_out4);
  Multiplexer #(.width(4), .enable("false")) multiplexer_2 (
    .in1(register_1_q), .out(ALU_Control), .sel(or_2_out));  // open: in0
  or or_3 (Load, decoder_1_out10, Memory_Read);
  or or_4 (RegWrite, or_2_out, decoder_1_out10, Memory_Read);
  or or_5 (PCwrite, decoder_1_out1, decoder_1_out2, decoder_1_out3, decoder_1_out4, PCmux, decoder_1_out10, Memory_Write, Branch);

  assign Immediate = in_1[7];
  assign Store = Memory_Write;
endmodule

module Register_File (
  input  [19:0] Data_in,
  input  Load,
  input  [3:0] Adress_A,
  input  [3:0] Input,
  input  [3:0] Adress_B,
  input  Clock,
  output [19:0] Address_A_out,
  output [19:0] Address_B_out
);

  wire and_1_out, and_2_out, and_3_out, and_4_out, and_5_out, and_6_out, and_7_out, and_8_out, and_9_out,
       and_10_out, and_11_out, and_12_out, and_13_out, and_14_out, and_15_out, and_16_out, decoder_1_out0,
       decoder_1_out1, decoder_1_out2, decoder_1_out3, decoder_1_out4, decoder_1_out5, decoder_1_out6,
       decoder_1_out7, decoder_1_out8, decoder_1_out9, decoder_1_out10, decoder_1_out11, decoder_1_out12,
       decoder_1_out13, decoder_1_out14, decoder_1_out15;
  wire [19:0] register_1_q, register_2_q, register_3_q, register_4_q, register_5_q, register_6_q,
       register_7_q, register_8_q, register_9_q, register_10_q, register_11_q, register_12_q, register_13_q,
       register_14_q, register_15_q, register_16_q;

  Decoder #(.select(4), .enable("false")) decoder_1 (
    .out0(decoder_1_out0), .out1(decoder_1_out1), .out2(decoder_1_out2), .out3(decoder_1_out3),
    .out4(decoder_1_out4), .out5(decoder_1_out5), .out6(decoder_1_out6), .out7(decoder_1_out7),
    .out8(decoder_1_out8), .out9(decoder_1_out9), .out10(decoder_1_out10), .out11(decoder_1_out11),
    .out12(decoder_1_out12), .out13(decoder_1_out13), .out14(decoder_1_out14), .out15(decoder_1_out15),
    .sel(Input));
  and and_1 (and_1_out, Load, decoder_1_out0);
  and and_2 (and_2_out, Load, decoder_1_out1);
  and and_3 (and_3_out, Load, decoder_1_out2);
  and and_4 (and_4_out, Load, decoder_1_out3);
  Register #(.width(20)) register_1 (.D(Data_in), .en(and_1_out), .Q(register_1_q), .clk(Clock));  // open: clr
  Register #(.width(20)) register_2 (.D(Data_in), .en(and_2_out), .Q(register_2_q), .clk(Clock));  // open: clr
  Register #(.width(20)) register_3 (.D(Data_in), .en(and_3_out), .Q(register_3_q), .clk(Clock));  // open: clr
  Register #(.width(20)) register_4 (.D(Data_in), .en(and_4_out), .Q(register_4_q), .clk(Clock));  // open: clr
  and and_5 (and_5_out, Load, decoder_1_out4);
  and and_6 (and_6_out, Load, decoder_1_out5);
  and and_7 (and_7_out, Load, decoder_1_out6);
  and and_8 (and_8_out, Load, decoder_1_out7);
  Register #(.width(20)) register_5 (.D(Data_in), .en(and_5_out), .Q(register_5_q), .clk(Clock));  // open: clr
  Register #(.width(20)) register_6 (.D(Data_in), .en(and_6_out), .Q(register_6_q), .clk(Clock));  // open: clr
  Register #(.width(20)) register_7 (.D(Data_in), .en(and_7_out), .Q(register_7_q), .clk(Clock));  // open: clr
  Register #(.width(20)) register_8 (.D(Data_in), .en(and_8_out), .Q(register_8_q), .clk(Clock));  // open: clr
  and and_9 (and_9_out, Load, decoder_1_out8);
  and and_10 (and_10_out, Load, decoder_1_out9);
  and and_11 (and_11_out, Load, decoder_1_out10);
  and and_12 (and_12_out, Load, decoder_1_out11);
  Register #(.width(20)) register_9 (.D(Data_in), .en(and_9_out), .Q(register_9_q), .clk(Clock));  // open: clr
  Register #(.width(20)) register_10 (.D(Data_in), .en(and_10_out), .Q(register_10_q), .clk(Clock));  // open: clr
  Register #(.width(20)) register_11 (.D(Data_in), .en(and_11_out), .Q(register_11_q), .clk(Clock));  // open: clr
  Register #(.width(20)) register_12 (.D(Data_in), .en(and_12_out), .Q(register_12_q), .clk(Clock));  // open: clr
  and and_13 (and_13_out, Load, decoder_1_out12);
  and and_14 (and_14_out, Load, decoder_1_out13);
  and and_15 (and_15_out, Load, decoder_1_out14);
  and and_16 (and_16_out, Load, decoder_1_out15);
  Register #(.width(20)) register_13 (.D(Data_in), .en(and_13_out), .Q(register_13_q), .clk(Clock));  // open: clr
  Register #(.width(20)) register_14 (.D(Data_in), .en(and_14_out), .Q(register_14_q), .clk(Clock));  // open: clr
  Register #(.width(20)) register_15 (.D(Data_in), .en(and_15_out), .Q(register_15_q), .clk(Clock));  // open: clr
  Register #(.width(20)) register_16 (.D(Data_in), .en(and_16_out), .Q(register_16_q), .clk(Clock));  // open: clr
  Multiplexer #(.select(4), .width(20), .enable("false")) multiplexer_1 (
    .in0(register_1_q), .in1(register_2_q), .in2(register_3_q), .in3(register_4_q), .in4(register_5_q),
    .in5(register_6_q), .in6(register_7_q), .in7(register_8_q), .in8(register_9_q), .in9(register_10_q),
    .in10(register_12_q), .in11(register_11_q), .in12(register_13_q), .in13(register_14_q),
    .in14(register_15_q), .in15(register_16_q), .out(Address_A_out), .sel(Adress_A));
  Multiplexer #(.select(4), .width(20), .enable("false")) multiplexer_2 (
    .in0(register_1_q), .in1(register_2_q), .in2(register_3_q), .in3(register_4_q), .in4(register_5_q),
    .in5(register_6_q), .in6(register_7_q), .in7(register_8_q), .in8(register_9_q), .in9(register_10_q),
    .in10(register_12_q), .in11(register_11_q), .in12(register_13_q), .in13(register_14_q),
    .in14(register_15_q), .in15(register_16_q), .out(Address_B_out), .sel(Adress_B));
endmodule

// Comparator
module _1_bit_Comparator (
  input  a,
  input  b,
  input  eq_in,
  input  gt_in,
  input  lt_in,
  output eq_out,
  output gt_out,
  output lt_out
);

  wire and_1_out, and_2_out, not_1_out, not_2_out, xnor_1_out;

  not not_1 (not_1_out, b);
  not not_2 (not_2_out, a);
  and and_1 (and_1_out, a, eq_in, not_1_out);
  and and_2 (and_2_out, b, not_2_out, eq_in);
  xnor xnor_1 (xnor_1_out, a, b);
  or or_1 (gt_out, and_1_out, gt_in);
  or or_2 (lt_out, and_2_out, lt_in);
  and and_3 (eq_out, xnor_1_out, eq_in);
endmodule

// Comparator
module _4_bit_Comparator (
  input  [3:0] B,
  input  [3:0] A,
  input  eq_in,
  input  gt_in,
  input  lt_in,
  output out_6,
  output out_7,
  output out_8
);

  wire n1_bit_comparator_1_eq_out, n1_bit_comparator_1_gt_out, n1_bit_comparator_1_lt_out,
       n1_bit_comparator_2_eq_out, n1_bit_comparator_2_gt_out, n1_bit_comparator_2_lt_out,
       n1_bit_comparator_3_eq_out, n1_bit_comparator_3_gt_out, n1_bit_comparator_3_lt_out;

  _1_bit_Comparator u_1_bit_comparator_1 (
    .a(A[3]), .b(B[3]), .eq_in(eq_in), .gt_in(gt_in), .lt_in(lt_in), .eq_out(n1_bit_comparator_1_eq_out),
    .gt_out(n1_bit_comparator_1_gt_out), .lt_out(n1_bit_comparator_1_lt_out));
  _1_bit_Comparator u_1_bit_comparator_2 (
    .a(A[2]), .b(B[2]), .eq_in(n1_bit_comparator_1_eq_out), .gt_in(n1_bit_comparator_1_gt_out),
    .lt_in(n1_bit_comparator_1_lt_out), .eq_out(n1_bit_comparator_2_eq_out),
    .gt_out(n1_bit_comparator_2_gt_out), .lt_out(n1_bit_comparator_2_lt_out));
  _1_bit_Comparator u_1_bit_comparator_3 (
    .a(A[1]), .b(B[1]), .eq_in(n1_bit_comparator_2_eq_out), .gt_in(n1_bit_comparator_2_gt_out),
    .lt_in(n1_bit_comparator_2_lt_out), .eq_out(n1_bit_comparator_3_eq_out),
    .gt_out(n1_bit_comparator_3_gt_out), .lt_out(n1_bit_comparator_3_lt_out));
  _1_bit_Comparator u_1_bit_comparator_4 (
    .a(A[0]), .b(B[0]), .eq_in(n1_bit_comparator_3_eq_out), .gt_in(n1_bit_comparator_3_gt_out),
    .lt_in(n1_bit_comparator_3_lt_out), .eq_out(out_6), .gt_out(out_7), .lt_out(out_8));
endmodule

// Comp
module _20_bit_Comparator (
  input  [19:0] A,
  input  [19:0] B,
  output [2:0] out_3
);

  wire n4_bit_comparator_1_out_6, n4_bit_comparator_1_out_7, n4_bit_comparator_1_out_8,
       n4_bit_comparator_2_out_6, n4_bit_comparator_2_out_7, n4_bit_comparator_2_out_8,
       n4_bit_comparator_3_out_6, n4_bit_comparator_3_out_7, n4_bit_comparator_3_out_8,
       n4_bit_comparator_4_out_6, n4_bit_comparator_4_out_7, n4_bit_comparator_4_out_8;

  _4_bit_Comparator u_4_bit_comparator_1 (
    .B(B[19:16]), .out_6(n4_bit_comparator_1_out_6), .out_7(n4_bit_comparator_1_out_7),
    .out_8(n4_bit_comparator_1_out_8), .A(A[19:16]), .eq_in(1'b1), .gt_in(1'b0), .lt_in(1'b0));
  _4_bit_Comparator u_4_bit_comparator_2 (
    .B(B[15:12]), .out_6(n4_bit_comparator_2_out_6), .out_7(n4_bit_comparator_2_out_7),
    .out_8(n4_bit_comparator_2_out_8), .A(A[15:12]), .eq_in(n4_bit_comparator_1_out_6),
    .gt_in(n4_bit_comparator_1_out_7), .lt_in(n4_bit_comparator_1_out_8));
  _4_bit_Comparator u_4_bit_comparator_3 (
    .B(B[11:8]), .out_6(n4_bit_comparator_3_out_6), .out_7(n4_bit_comparator_3_out_7),
    .out_8(n4_bit_comparator_3_out_8), .A(A[11:8]), .eq_in(n4_bit_comparator_2_out_6),
    .gt_in(n4_bit_comparator_2_out_7), .lt_in(n4_bit_comparator_2_out_8));
  _4_bit_Comparator u_4_bit_comparator_4 (
    .B(B[7:4]), .out_6(n4_bit_comparator_4_out_6), .out_7(n4_bit_comparator_4_out_7),
    .out_8(n4_bit_comparator_4_out_8), .A(A[7:4]), .eq_in(n4_bit_comparator_3_out_6),
    .gt_in(n4_bit_comparator_3_out_7), .lt_in(n4_bit_comparator_3_out_8));
  _4_bit_Comparator u_4_bit_comparator_5 (
    .B(B[3:0]), .out_6(out_3[1]), .out_7(out_3[2]), .out_8(out_3[0]), .A(A[3:0]),
    .eq_in(n4_bit_comparator_4_out_6), .gt_in(n4_bit_comparator_4_out_7), .lt_in(n4_bit_comparator_4_out_8));
endmodule

module Sign_Extend_7_20 (
  input  [6:0] Immediate_value,
  output [19:0] Extend_number
);


  assign Extend_number = {{14{Immediate_value[0]}}, Immediate_value[1], Immediate_value[2], Immediate_value[3], Immediate_value[4], Immediate_value[5], Immediate_value[6]};
endmodule

module _1_bit_Subtractor (
  input  wi,
  input  A,
  input  B,
  output Difference,
  output wo
);

  wire and_1_out, and_2_out, and_3_out, and_4_out, and_5_out, and_6_out, not_1_out, not_2_out, not_3_out,
       not_4_out, not_5_out, not_6_out, not_7_out, not_8_out, not_9_out;

  not not_1 (not_1_out, wi);
  not not_2 (not_2_out, A);
  not not_3 (not_3_out, wi);
  not not_4 (not_4_out, B);
  not not_5 (not_5_out, A);
  not not_6 (not_6_out, B);
  not not_7 (not_7_out, wi);
  not not_8 (not_8_out, A);
  not not_9 (not_9_out, B);
  and and_1 (and_1_out, not_1_out, not_2_out, B);
  and and_2 (and_2_out, not_3_out, A, not_4_out);
  and and_3 (and_3_out, wi, not_5_out, not_6_out);
  and and_4 (and_4_out, wi, A, B);
  and and_5 (and_5_out, not_7_out, not_8_out, B);
  and and_6 (and_6_out, wi, A, not_9_out);
  or or_1 (Difference, and_1_out, and_2_out, and_3_out, and_4_out);
  or or_2 (wo, and_5_out, and_6_out);
endmodule

module _4_bit_Subtractor (
  input  [3:0] A,
  input  [3:0] B,
  input  wi,
  output out_4,
  output [3:0] out_5
);

  wire n1_bit_subtractor_2_wo, n1_bit_subtractor_3_wo, n1_bit_subtractor_4_wo;

  _1_bit_Subtractor u_1_bit_subtractor_1 (
    .wi(n1_bit_subtractor_2_wo), .A(A[3]), .B(B[3]), .Difference(out_5[3]), .wo(out_4));
  _1_bit_Subtractor u_1_bit_subtractor_2 (
    .wi(n1_bit_subtractor_3_wo), .A(A[2]), .B(B[2]), .Difference(out_5[2]), .wo(n1_bit_subtractor_2_wo));
  _1_bit_Subtractor u_1_bit_subtractor_3 (
    .wi(n1_bit_subtractor_4_wo), .A(A[1]), .B(B[1]), .Difference(out_5[1]), .wo(n1_bit_subtractor_3_wo));
  _1_bit_Subtractor u_1_bit_subtractor_4 (
    .wi(wi), .A(A[0]), .B(B[0]), .Difference(out_5[0]), .wo(n1_bit_subtractor_4_wo));
endmodule

module _20_bit_Subtractor (
  input  [19:0] in_1,
  input  [19:0] in_2,
  output out_3,
  output [19:0] out_4
);

  wire n4_bit_subtractor_2_out_4, n4_bit_subtractor_3_out_4, n4_bit_subtractor_4_out_4,
       n4_bit_subtractor_5_out_4;

  _4_bit_Subtractor u_4_bit_subtractor_1 (
    .A(in_2[19:16]), .B(in_1[19:16]), .wi(n4_bit_subtractor_2_out_4), .out_4(out_3), .out_5(out_4[19:16]));
  _4_bit_Subtractor u_4_bit_subtractor_2 (
    .A(in_2[15:12]), .B(in_1[15:12]), .wi(n4_bit_subtractor_3_out_4), .out_4(n4_bit_subtractor_2_out_4),
    .out_5(out_4[15:12]));
  _4_bit_Subtractor u_4_bit_subtractor_3 (
    .A(in_2[11:8]), .B(in_1[11:8]), .wi(n4_bit_subtractor_4_out_4), .out_4(n4_bit_subtractor_3_out_4),
    .out_5(out_4[11:8]));
  _4_bit_Subtractor u_4_bit_subtractor_4 (
    .A(in_2[7:4]), .B(in_1[7:4]), .wi(n4_bit_subtractor_5_out_4), .out_4(n4_bit_subtractor_4_out_4),
    .out_5(out_4[7:4]));
  _4_bit_Subtractor u_4_bit_subtractor_5 (
    .A(in_2[3:0]), .B(in_1[3:0]), .wi(1'b0), .out_4(n4_bit_subtractor_5_out_4), .out_5(out_4[3:0]));
endmodule

module Branch (
  input  [2:0] nzp,
  input  [19:0] OP1,
  input  [19:0] OP2,
  output Condition
);

  wire and_1_out, and_2_out, and_3_out, and_4_out, and_5_out, and_6_out, and_7_out, decoder_1_out1,
       decoder_1_out2, decoder_1_out3, decoder_1_out4, decoder_1_out6, decoder_2_out1, decoder_2_out2,
       decoder_2_out4, or_1_out, or_2_out;
  wire [2:0] n20_bit_comparator_1_out_3;

  Decoder #(.select(3), .enable("false")) decoder_1 (
    .out1(decoder_1_out1), .out2(decoder_1_out2), .out3(decoder_1_out3), .out4(decoder_1_out4),
    .out6(decoder_1_out6), .sel(nzp));  // open: out0, out5, out7
  Decoder #(.select(3), .enable("false")) decoder_2 (
    .out1(decoder_2_out1), .out2(decoder_2_out2), .out4(decoder_2_out4), .sel(n20_bit_comparator_1_out_3));  // open: out0, out3, out5, out6, out7
  _20_bit_Comparator u_20_bit_comparator_1 (.A(OP1), .B(OP2), .out_3(n20_bit_comparator_1_out_3));
  and and_1 (and_1_out, decoder_1_out2, decoder_2_out2);
  and and_2 (and_2_out, decoder_1_out4, decoder_2_out4);
  and and_3 (and_3_out, decoder_1_out1, decoder_2_out1);
  and and_4 (and_4_out, decoder_2_out4, decoder_1_out6);
  and and_5 (and_5_out, decoder_2_out2, decoder_1_out6);
  and and_6 (and_6_out, decoder_2_out1, decoder_1_out3);
  and and_7 (and_7_out, decoder_2_out2, decoder_1_out3);
  or or_1 (or_1_out, and_4_out, and_5_out);
  or or_2 (or_2_out, and_6_out, and_7_out);
  or or_3 (Condition, and_1_out, and_2_out, and_3_out, or_1_out, or_2_out);
endmodule

// Extender
module Sign_Extender_16_20 (
  input  [15:0] in_1,
  output [19:0] out_2
);


  assign out_2 = {{5{in_1[15]}}, in_1[14:0]};
endmodule

// Extnd
module Extender_5_20 (
  input  [4:0] in_1,
  output [19:0] out_2
);


  assign out_2 = {{16{in_1[4]}}, in_1[3:0]};
endmodule
